// Logisim project BinarySpaghettiSortCircuit.circ as structural Verilog: 2 circuits, main circuit main
module main (
  input  [2:0] in_1,
  input  [2:0] in_2,
  input  [2:0] in_3,
  input  [2:0] in_4,
  output [4:0] out_5,
  output [4:0] out_6,
  output [4:0] out_7,
  output [4:0] out_8
);

  wire n7447_1_pin6, n7447_1_pin9, n7447_1_pin10, n7447_1_pin11, n7447_1_pin12, n7447_1_pin13, n7447_1_pin14,
       n7447_1_pin15, n7447_2_pin9, n7447_2_pin10, n7447_2_pin11, n7447_2_pin12, n7447_2_pin13,
       n7447_2_pin14, n7447_2_pin15, n7447_3_pin9, n7447_3_pin10, n7447_3_pin11, n7447_3_pin12,
       n7447_3_pin13, n7447_3_pin14, n7447_3_pin15, n7447_4_pin9, n7447_4_pin10, n7447_4_pin11,
       n7447_4_pin12, n7447_4_pin13, n7447_4_pin14, n7447_4_pin15, n7447_5_pin6, n7447_5_pin9, n7447_5_pin10,
       n7447_5_pin11, n7447_5_pin12, n7447_5_pin13, n7447_5_pin14, n7447_5_pin15, n7447_6_pin9,
       n7447_6_pin10, n7447_6_pin11, n7447_6_pin12, n7447_6_pin13, n7447_6_pin14, n7447_6_pin15,
       n7447_7_pin9, n7447_7_pin10, n7447_7_pin11, n7447_7_pin12, n7447_7_pin13, n7447_7_pin14,
       n7447_7_pin15, n7447_8_pin9, n7447_8_pin10, n7447_8_pin11, n7447_8_pin12, n7447_8_pin13,
       n7447_8_pin14, n7447_8_pin15;
  wire [2:0] myloop2_1_position1, myloop2_1_position2, myloop2_1_position3, myloop2_1_position4,
       myloop2_1_updatedcounter, myloop2_2_position1, myloop2_2_position2, myloop2_2_position3,
       myloop2_2_position4, myloop2_2_updatedcounter, myloop2_3_position1, myloop2_3_position2,
       myloop2_3_position3, myloop2_3_position4, myloop2_3_updatedcounter, myloop2_4_position1,
       myloop2_4_position2, myloop2_4_position3, myloop2_4_position4, myloop2_4_updatedcounter,
       myloop2_5_position1, myloop2_5_position2, myloop2_5_position3, myloop2_5_position4, n7447_5_pin7,
       n7447_6_pin7, n7447_7_pin7, n7447_8_pin7, subtractor_1_out, subtractor_2_out, subtractor_3_out,
       subtractor_4_out;

  _7447 u_7447_1 (
    .pin1(in_1[1]), .pin2(in_1[2]), .pin6(n7447_1_pin6), .pin7(in_1[0]), .pin15(n7447_1_pin15),
    .pin14(n7447_1_pin14), .pin13(n7447_1_pin13), .pin12(n7447_1_pin12), .pin11(n7447_1_pin11),
    .pin10(n7447_1_pin10), .pin9(n7447_1_pin9));  // open: pin3, pin4, pin5
  Subtractor #(.width(3)) subtractor_1 (.a(in_1), .b(3'b001), .out(subtractor_1_out));  // open: bin, bout
  Subtractor #(.width(3)) subtractor_2 (.a(in_2), .b(3'b001), .out(subtractor_2_out));  // open: bin, bout
  Subtractor #(.width(3)) subtractor_3 (.a(in_3), .b(3'b001), .out(subtractor_3_out));  // open: bin, bout
  Subtractor #(.width(3)) subtractor_4 (.a(in_4), .b(3'b001), .out(subtractor_4_out));  // open: bin, bout
  _7_Segment_Display u_7_segment_display_1 (
    .g(n7447_1_pin14), .f(n7447_1_pin15), .a(n7447_1_pin13), .b(n7447_1_pin12), .e(n7447_1_pin9),
    .d(n7447_1_pin10), .c(n7447_1_pin11));  // open: dp
  Shifter #(.width(5)) shifter_1 (.in(5'b00001), .\dist (subtractor_1_out), .out(out_5));
  Shifter #(.width(5)) shifter_2 (.in(5'b00001), .\dist (subtractor_2_out), .out(out_6));
  Shifter #(.width(5)) shifter_3 (.in(5'b00001), .\dist (subtractor_3_out), .out(out_7));
  Shifter #(.width(5)) shifter_4 (.in(5'b00001), .\dist (subtractor_4_out), .out(out_8));
  _7447 u_7447_2 (
    .pin1(in_2[1]), .pin2(in_2[2]), .pin6(n7447_1_pin6), .pin7(in_2[0]), .pin15(n7447_2_pin15),
    .pin14(n7447_2_pin14), .pin13(n7447_2_pin13), .pin12(n7447_2_pin12), .pin11(n7447_2_pin11),
    .pin10(n7447_2_pin10), .pin9(n7447_2_pin9));  // open: pin3, pin4, pin5
  _7_Segment_Display u_7_segment_display_2 (
    .g(n7447_2_pin14), .f(n7447_2_pin15), .a(n7447_2_pin13), .b(n7447_2_pin12), .e(n7447_2_pin9),
    .d(n7447_2_pin10), .c(n7447_2_pin11));  // open: dp
  _7447 u_7447_3 (
    .pin1(in_3[1]), .pin2(in_3[2]), .pin6(n7447_1_pin6), .pin7(in_3[0]), .pin15(n7447_3_pin15),
    .pin14(n7447_3_pin14), .pin13(n7447_3_pin13), .pin12(n7447_3_pin12), .pin11(n7447_3_pin11),
    .pin10(n7447_3_pin10), .pin9(n7447_3_pin9));  // open: pin3, pin4, pin5
  _7_Segment_Display u_7_segment_display_3 (
    .g(n7447_3_pin14), .f(n7447_3_pin15), .a(n7447_3_pin13), .b(n7447_3_pin12), .e(n7447_3_pin9),
    .d(n7447_3_pin10), .c(n7447_3_pin11));  // open: dp
  _7447 u_7447_4 (
    .pin1(in_4[1]), .pin2(in_4[2]), .pin6(n7447_1_pin6), .pin7(in_4[0]), .pin15(n7447_4_pin15),
    .pin14(n7447_4_pin14), .pin13(n7447_4_pin13), .pin12(n7447_4_pin12), .pin11(n7447_4_pin11),
    .pin10(n7447_4_pin10), .pin9(n7447_4_pin9));  // open: pin3, pin4, pin5
  _7_Segment_Display u_7_segment_display_4 (
    .g(n7447_4_pin14), .f(n7447_4_pin15), .a(n7447_4_pin13), .b(n7447_4_pin12), .e(n7447_4_pin9),
    .d(n7447_4_pin10), .c(n7447_4_pin11));  // open: dp
  _7447 u_7447_5 (
    .pin1(n7447_5_pin7[1]), .pin2(n7447_5_pin7[2]), .pin6(n7447_5_pin6), .pin7(n7447_5_pin7[0]),
    .pin15(n7447_5_pin15), .pin14(n7447_5_pin14), .pin13(n7447_5_pin13), .pin12(n7447_5_pin12),
    .pin11(n7447_5_pin11), .pin10(n7447_5_pin10), .pin9(n7447_5_pin9));  // open: pin3, pin4, pin5
  assign n7447_5_pin7 = myloop2_1_position1 | myloop2_2_position1 | myloop2_3_position1 | myloop2_4_position1 | myloop2_5_position1;  // OR_Gate or_1, 3 bits wide
  _7_Segment_Display u_7_segment_display_5 (
    .g(n7447_5_pin14), .f(n7447_5_pin15), .a(n7447_5_pin13), .b(n7447_5_pin12), .e(n7447_5_pin9),
    .d(n7447_5_pin10), .c(n7447_5_pin11));  // open: dp
  LED led_1 (.in(out_5[0]));
  LED led_2 (.in(out_6[0]));
  LED led_3 (.in(out_5[1]));
  LED led_4 (.in(out_6[1]));
  LED led_5 (.in(out_5[2]));
  LED led_6 (.in(out_6[2]));
  LED led_7 (.in(out_5[3]));
  LED led_8 (.in(out_6[3]));
  LED led_9 (.in(out_5[4]));
  LED led_10 (.in(out_6[4]));
  _7447 u_7447_6 (
    .pin1(n7447_6_pin7[1]), .pin2(n7447_6_pin7[2]), .pin6(n7447_5_pin6), .pin7(n7447_6_pin7[0]),
    .pin15(n7447_6_pin15), .pin14(n7447_6_pin14), .pin13(n7447_6_pin13), .pin12(n7447_6_pin12),
    .pin11(n7447_6_pin11), .pin10(n7447_6_pin10), .pin9(n7447_6_pin9));  // open: pin3, pin4, pin5
  LED led_11 (.in(out_7[0]));
  LED led_12 (.in(out_8[0]));
  LED led_13 (.in(out_7[1]));
  LED led_14 (.in(out_8[1]));
  LED led_15 (.in(out_7[2]));
  LED led_16 (.in(out_8[2]));
  LED led_17 (.in(out_7[3]));
  LED led_18 (.in(out_8[3]));
  LED led_19 (.in(out_7[4]));
  LED led_20 (.in(out_8[4]));
  assign n7447_6_pin7 = myloop2_1_position2 | myloop2_2_position2 | myloop2_3_position2 | myloop2_4_position2 | myloop2_5_position2;  // OR_Gate or_2, 3 bits wide
  _7_Segment_Display u_7_segment_display_6 (
    .g(n7447_6_pin14), .f(n7447_6_pin15), .a(n7447_6_pin13), .b(n7447_6_pin12), .e(n7447_6_pin9),
    .d(n7447_6_pin10), .c(n7447_6_pin11));  // open: dp
  _7447 u_7447_7 (
    .pin1(n7447_7_pin7[1]), .pin2(n7447_7_pin7[2]), .pin6(n7447_5_pin6), .pin7(n7447_7_pin7[0]),
    .pin15(n7447_7_pin15), .pin14(n7447_7_pin14), .pin13(n7447_7_pin13), .pin12(n7447_7_pin12),
    .pin11(n7447_7_pin11), .pin10(n7447_7_pin10), .pin9(n7447_7_pin9));  // open: pin3, pin4, pin5
  assign n7447_7_pin7 = myloop2_1_position3 | myloop2_2_position3 | myloop2_3_position3 | myloop2_4_position3 | myloop2_5_position3;  // OR_Gate or_3, 3 bits wide
  _7_Segment_Display u_7_segment_display_7 (
    .g(n7447_7_pin14), .f(n7447_7_pin15), .a(n7447_7_pin13), .b(n7447_7_pin12), .e(n7447_7_pin9),
    .d(n7447_7_pin10), .c(n7447_7_pin11));  // open: dp
  _7447 u_7447_8 (
    .pin1(n7447_8_pin7[1]), .pin2(n7447_8_pin7[2]), .pin6(n7447_5_pin6), .pin7(n7447_8_pin7[0]),
    .pin15(n7447_8_pin15), .pin14(n7447_8_pin14), .pin13(n7447_8_pin13), .pin12(n7447_8_pin12),
    .pin11(n7447_8_pin11), .pin10(n7447_8_pin10), .pin9(n7447_8_pin9));  // open: pin3, pin4, pin5
  assign n7447_8_pin7 = myloop2_1_position4 | myloop2_2_position4 | myloop2_3_position4 | myloop2_4_position4 | myloop2_5_position4;  // OR_Gate or_4, 3 bits wide
  _7_Segment_Display u_7_segment_display_8 (
    .g(n7447_8_pin14), .f(n7447_8_pin15), .a(n7447_8_pin13), .b(n7447_8_pin12), .e(n7447_8_pin9),
    .d(n7447_8_pin10), .c(n7447_8_pin11));  // open: dp
  MyLoop2 myloop2_1 (
    .Counter(3'b000), .IndexValue({out_5[0], out_6[0], out_7[0], out_8[0]}), .Spaghetto1(in_4),
    .Spaghetto2(in_3), .Spaghetto3(in_2), .Spaghetto4(in_1), .UpdatedCounter(myloop2_1_updatedcounter),
    .Position1(myloop2_1_position1), .Position2(myloop2_1_position2), .Position3(myloop2_1_position3),
    .Position4(myloop2_1_position4));
  MyLoop2 myloop2_2 (
    .Counter(myloop2_1_updatedcounter), .IndexValue({out_5[1], out_6[1], out_7[1], out_8[1]}),
    .Spaghetto1(in_4), .Spaghetto2(in_3), .Spaghetto3(in_2), .Spaghetto4(in_1),
    .UpdatedCounter(myloop2_2_updatedcounter), .Position1(myloop2_2_position1),
    .Position2(myloop2_2_position2), .Position3(myloop2_2_position3), .Position4(myloop2_2_position4));
  MyLoop2 myloop2_3 (
    .Counter(myloop2_2_updatedcounter), .IndexValue({out_5[2], out_6[2], out_7[2], out_8[2]}),
    .Spaghetto1(in_4), .Spaghetto2(in_3), .Spaghetto3(in_2), .Spaghetto4(in_1),
    .UpdatedCounter(myloop2_3_updatedcounter), .Position1(myloop2_3_position1),
    .Position2(myloop2_3_position2), .Position3(myloop2_3_position3), .Position4(myloop2_3_position4));
  MyLoop2 myloop2_4 (
    .Counter(myloop2_3_updatedcounter), .IndexValue({out_5[3], out_6[3], out_7[3], out_8[3]}),
    .Spaghetto1(in_4), .Spaghetto2(in_3), .Spaghetto3(in_2), .Spaghetto4(in_1),
    .UpdatedCounter(myloop2_4_updatedcounter), .Position1(myloop2_4_position1),
    .Position2(myloop2_4_position2), .Position3(myloop2_4_position3), .Position4(myloop2_4_position4));
  MyLoop2 myloop2_5 (
    .Counter(myloop2_4_updatedcounter), .IndexValue({out_5[4], out_6[4], out_7[4], out_8[4]}),
    .Spaghetto1(in_4), .Spaghetto2(in_3), .Spaghetto3(in_2), .Spaghetto4(in_1),
    .Position1(myloop2_5_position1), .Position2(myloop2_5_position2), .Position3(myloop2_5_position3),
    .Position4(myloop2_5_position4));  // open: UpdatedCounter
  // also tied to GND on the sheet: {n7447_1_pin6, n7447_5_pin6}

  // Notes on the sheet:
  //   Number from 1 to 5
  //   Head (1) to shift
  //   We need to subtract 1
  //   INPUT: Numbers to sort from 1 to 5
  //   Number from 1 to 5
  //   Number from 1 to 5
  //   Spaghettization
  //   Binary Spaghetti Sort Algorithm as an Electrical Circuit
  //   Number from 1 to 5
  //   1 is at
  //   2 is at
  //   3 is at
  //   4 is at
  //   5 is at
  //   Binary Spaghetti Heads Index
endmodule

module MyLoop2 (
  input  [2:0] Counter,
  input  [3:0] IndexValue,
  input  [2:0] Spaghetto1,
  input  [2:0] Spaghetto2,
  input  [2:0] Spaghetto3,
  input  [2:0] Spaghetto4,
  output [2:0] UpdatedCounter,
  output [2:0] Position1,
  output [2:0] Position2,
  output [2:0] Position3,
  output [2:0] Position4
);

  wire [0:0] bitfinder_1_found, bitfinder_3_found, bitfinder_4_found;
  wire [1:0] bitfinder_1_index, bitfinder_2_index, bitfinder_3_index, bitfinder_4_index, pla_1_out,
       pla_2_out, pla_3_out, pla_4_out, subtractor_1_out, subtractor_2_out, subtractor_3_out,
       subtractor_4_out, subtractor_5_out, subtractor_6_out;
  wire [1:1] bitfinder_2_found;
  wire [2:0] adder_1_out, adder_2_out, adder_3_out, demultiplexer_1_out0, demultiplexer_1_out1,
       demultiplexer_1_out2, demultiplexer_1_out3, demultiplexer_2_out0, demultiplexer_2_out1,
       demultiplexer_2_out2, demultiplexer_2_out3, demultiplexer_3_out0, demultiplexer_3_out1,
       demultiplexer_3_out2, demultiplexer_3_out3, demultiplexer_4_out0, demultiplexer_4_out1,
       demultiplexer_4_out2, demultiplexer_4_out3, multiplexer_1_out, multiplexer_3_out, multiplexer_4_out,
       multiplexer_6_out, multiplexer_10_out, multiplexer_13_out, multiplexer_15_out, multiplexer_16_out,
       subtractor_7_out, subtractor_8_out;
  wire [2:2] subtractor_1_out_2, subtractor_2_out_2;
  wire [3:0] multiplexer_2_out, multiplexer_5_out, multiplexer_8_out, multiplexer_14_out, shifter_1_out,
       shifter_2_out, shifter_3_out, shifter_4_out, xor_1_out, xor_2_out, xor_3_out;

  BitFinder #(.width(4)) bitfinder_1 (.in(IndexValue), .index(bitfinder_1_index), .found(bitfinder_1_found[0]));
  Shifter #(.width(4)) shifter_1 (.in(4'b0001), .\dist (bitfinder_1_index), .out(shifter_1_out));
  Multiplexer #(.select(2), .width(3)) multiplexer_1 (
    .in0(Spaghetto1), .in1(Spaghetto2), .in2(Spaghetto3), .in3(Spaghetto4), .out(multiplexer_1_out),
    .sel(bitfinder_1_index));
  Multiplexer #(.width(4)) multiplexer_2 (
    .in0(4'b0000), .in1(shifter_1_out), .out(multiplexer_2_out), .sel(bitfinder_1_found[0]));
  Adder #(.width(3)) adder_1 (.a(Counter), .b({2'b00, bitfinder_1_found[0]}), .out(adder_1_out));  // open: cin, cout
  Multiplexer #(.width(3)) multiplexer_3 (
    .in0(3'b000), .in1(multiplexer_1_out), .out(multiplexer_3_out), .sel(bitfinder_1_found[0]));
  Demultiplexer #(.select(2), .width(3)) demultiplexer_1 (
    .out0(demultiplexer_1_out0), .out1(demultiplexer_1_out1), .out2(demultiplexer_1_out2),
    .out3(demultiplexer_1_out3), .in(multiplexer_3_out), .sel(subtractor_1_out));
  assign xor_1_out = multiplexer_2_out ^ IndexValue;  // XOR_Gate xor_1, 4 bits wide
  Subtractor #(.width(3)) subtractor_1 (
    .a(adder_1_out), .b(3'b001), .out({subtractor_1_out_2[2], subtractor_1_out}));  // open: bin, bout
  PLA #(.in_width(4), .\table ("xxxx 00")) pla_1 (
    .in({bitfinder_4_found[0], bitfinder_3_found[0], bitfinder_2_found[1], bitfinder_1_found[0]}),
    .out(pla_1_out));
  PLA #(.in_width(4), .\table ("xxxx 01")) pla_2 (
    .in({bitfinder_4_found[0], bitfinder_3_found[0], bitfinder_2_found[1], bitfinder_1_found[0]}),
    .out(pla_2_out));
  BitFinder #(.width(4)) bitfinder_2 (.in(xor_1_out), .index(bitfinder_2_index), .found(bitfinder_2_found[1]));
  PLA #(.in_width(4), .\table ("xxxx 10")) pla_3 (
    .in({bitfinder_4_found[0], bitfinder_3_found[0], bitfinder_2_found[1], bitfinder_1_found[0]}),
    .out(pla_3_out));
  Shifter #(.width(4)) shifter_2 (.in(4'b0001), .\dist (bitfinder_2_index), .out(shifter_2_out));
  Multiplexer #(.select(2), .width(3)) multiplexer_4 (
    .in0(Spaghetto1), .in1(Spaghetto2), .in2(Spaghetto3), .in3(Spaghetto4), .out(multiplexer_4_out),
    .sel(bitfinder_2_index));
  PLA #(.in_width(4), .\table ("xxxx 11")) pla_4 (
    .in({bitfinder_4_found[0], bitfinder_3_found[0], bitfinder_2_found[1], bitfinder_1_found[0]}),
    .out(pla_4_out));
  Multiplexer #(.width(4)) multiplexer_5 (
    .in0(4'b0000), .in1(shifter_2_out), .out(multiplexer_5_out), .sel(bitfinder_2_found[1]));
  Multiplexer #(.width(3)) multiplexer_6 (
    .in0(3'b000), .in1(multiplexer_4_out), .out(multiplexer_6_out), .sel(bitfinder_2_found[1]));
  assign xor_2_out = multiplexer_5_out ^ xor_1_out;  // XOR_Gate xor_2, 4 bits wide
  Adder #(.width(3)) adder_2 (
    .a(adder_1_out), .b({2'b00, bitfinder_2_found[1]}), .out(adder_2_out));  // open: cin, cout
  Demultiplexer #(.select(2), .width(3)) demultiplexer_2 (
    .out0(demultiplexer_2_out0), .out1(demultiplexer_2_out1), .out2(demultiplexer_2_out2),
    .out3(demultiplexer_2_out3), .in(multiplexer_6_out), .sel(subtractor_2_out));
  BitFinder #(.width(4)) bitfinder_3 (.in(xor_2_out), .index(bitfinder_3_index), .found(bitfinder_3_found[0]));
  Subtractor #(.width(3)) subtractor_2 (
    .a(adder_2_out), .b(3'b001), .out({subtractor_2_out_2[2], subtractor_2_out}));  // open: bin, bout
  Shifter #(.width(4)) shifter_3 (.in(4'b0001), .\dist (bitfinder_3_index), .out(shifter_3_out));
  Multiplexer #(.select(2), .width(3)) multiplexer_7 (
    .in0(demultiplexer_1_out0), .in1(demultiplexer_2_out0), .in2(demultiplexer_3_out0),
    .in3(demultiplexer_4_out0), .out(Position1), .sel(subtractor_3_out));
  Multiplexer #(.width(4)) multiplexer_8 (
    .in0(4'b0000), .in1(shifter_3_out), .out(multiplexer_8_out), .sel(bitfinder_3_found[0]));
  Subtractor #(.width(2)) subtractor_3 (.a(pla_1_out), .b(Counter[1:0]), .out(subtractor_3_out));  // open: bin, bout
  Subtractor #(.width(2)) subtractor_4 (.a(pla_2_out), .b(Counter[1:0]), .out(subtractor_4_out));  // open: bin, bout
  Multiplexer #(.select(2), .width(3)) multiplexer_9 (
    .in0(demultiplexer_1_out1), .in1(demultiplexer_2_out1), .in2(demultiplexer_3_out1),
    .in3(demultiplexer_4_out1), .out(Position2), .sel(subtractor_4_out));
  Adder #(.width(3)) adder_3 (
    .a(adder_2_out), .b({2'b00, bitfinder_3_found[0]}), .out(adder_3_out));  // open: cin, cout
  Multiplexer #(.select(2), .width(3)) multiplexer_10 (
    .in0(Spaghetto1), .in1(Spaghetto2), .in2(Spaghetto3), .in3(Spaghetto4), .out(multiplexer_10_out),
    .sel(bitfinder_3_index));
  Subtractor #(.width(2)) subtractor_5 (.a(pla_3_out), .b(Counter[1:0]), .out(subtractor_5_out));  // open: bin, bout
  Multiplexer #(.select(2), .width(3)) multiplexer_11 (
    .in0(demultiplexer_1_out2), .in1(demultiplexer_2_out2), .in2(demultiplexer_3_out2),
    .in3(demultiplexer_4_out2), .out(Position3), .sel(subtractor_5_out));
  Subtractor #(.width(2)) subtractor_6 (.a(pla_4_out), .b(Counter[1:0]), .out(subtractor_6_out));  // open: bin, bout
  Multiplexer #(.select(2), .width(3)) multiplexer_12 (
    .in0(demultiplexer_1_out3), .in1(demultiplexer_2_out3), .in2(demultiplexer_3_out3),
    .in3(demultiplexer_4_out3), .out(Position4), .sel(subtractor_6_out));
  assign xor_3_out = multiplexer_8_out ^ xor_2_out;  // XOR_Gate xor_3, 4 bits wide
  Subtractor #(.width(3)) subtractor_7 (.a(adder_3_out), .b(3'b001), .out(subtractor_7_out));  // open: bin, bout
  Multiplexer #(.width(3)) multiplexer_13 (
    .in0(3'b000), .in1(multiplexer_10_out), .out(multiplexer_13_out), .sel(bitfinder_3_found[0]));
  Demultiplexer #(.select(2), .width(3)) demultiplexer_3 (
    .out0(demultiplexer_3_out0), .out1(demultiplexer_3_out1), .out2(demultiplexer_3_out2),
    .out3(demultiplexer_3_out3), .in(multiplexer_13_out), .sel(subtractor_7_out[1:0]));
  BitFinder #(.width(4)) bitfinder_4 (.in(xor_3_out), .index(bitfinder_4_index), .found(bitfinder_4_found[0]));
  Shifter #(.width(4)) shifter_4 (.in(4'b0001), .\dist (bitfinder_4_index), .out(shifter_4_out));
  Multiplexer #(.width(4)) multiplexer_14 (
    .in0(4'b0000), .in1(shifter_4_out), .out(multiplexer_14_out), .sel(bitfinder_4_found[0]));
  // XOR_Gate xor_4 has open pins: in0=multiplexer_14_out, in1=xor_3_out, out=open
  Adder #(.width(3)) adder_4 (
    .a(adder_3_out), .b({2'b00, bitfinder_4_found[0]}), .out(UpdatedCounter));  // open: cin, cout
  Subtractor #(.width(3)) subtractor_8 (.a(UpdatedCounter), .b(3'b001), .out(subtractor_8_out));  // open: bin, bout
  Multiplexer #(.select(2), .width(3)) multiplexer_15 (
    .in0(Spaghetto1), .in1(Spaghetto2), .in2(Spaghetto3), .in3(Spaghetto4), .out(multiplexer_15_out),
    .sel(bitfinder_4_index));
  Multiplexer #(.width(3)) multiplexer_16 (
    .in0(3'b000), .in1(multiplexer_15_out), .out(multiplexer_16_out), .sel(bitfinder_4_found[0]));
  Demultiplexer #(.select(2), .width(3)) demultiplexer_4 (
    .out0(demultiplexer_4_out0), .out1(demultiplexer_4_out1), .out2(demultiplexer_4_out2),
    .out3(demultiplexer_4_out3), .in(multiplexer_16_out), .sel(subtractor_8_out[1:0]));

  // Notes on the sheet:
  //   Counts position in result
  //   Sends number found to
  //   the right output below
  //   If no bit found sets XORs to zero
  //   Used to mask bits
  //   If number found
  //   position increases
  //   Binary Spaghetti Sort Algorithm as an Electrical Circuit - Sorting While Loop
  //   A series of plexers to pick the right number
  //   and send it to the right output port
  //   Outputs which positions were set
endmodule
